// Logisim project CPUSketch.circ as structural Verilog: 1 circuit, main circuit main
module main (
);

  wire [15:0] multiplexer_1_out, multiplexer_2_out, register_1_q, undriven;

  Multiplexer #(.width(16)) multiplexer_1 (.out(multiplexer_1_out));  // open: in0, in1, sel, en
  Register #(.width(16)) register_1 (.D(multiplexer_1_out), .Q(register_1_q));  // open: en, clk, clr
  Multiplexer #(.width(16)) multiplexer_2 (
    .in0(register_1_q), .in1(undriven), .out(multiplexer_2_out));  // open: sel, en
endmodule
