// Logisim project Parts.circ as structural Verilog: 1 circuit, main circuit main
module main (
  input  in_1,
  input  in_2,
  input  in_3,
  input  in_4,
  input  in_5,
  output out_6,
  output out_7
);

  wire multiplexer_1_out, xor_1_out;

  xor xor_1 (xor_1_out, in_1, 1'b1);
  not not_1 (out_6, xor_1_out);
  Multiplexer #(.enable("false")) multiplexer_1 (.in0(in_2), .in1(in_3), .out(multiplexer_1_out), .sel(in_5));
  Multiplexer #(.disabled(0), .enable("false")) multiplexer_2 (
    .in0(1'b0), .in1(multiplexer_1_out), .out(out_7), .sel(in_4));
endmodule
